// Logisim project cpu.circ as structural Verilog: 7 circuits, main circuit main
module main (
);

  wire clock_1_out, i_decode_1_beq_flag, i_decode_1_jmp_flag, i_decode_1_prnt_flag, i_decode_1_rst_flag,
       or_1_out, Reset_Display_out, Reset_out;
  wire [6:0] i_decode_1_prnt_register;
  wire [7:0] ram_1_data_2, register_1_q, register_2_q, register_3_q, register_4_q;
  wire [15:0] i_decode_1_jmp_address, programcounter_1_adress;
  wire [31:8] ram_1_data;

  Clock clock_1 (.out(clock_1_out));
  Button Reset (.out(Reset_out));
  Button Reset_Display (.out(Reset_Display_out));
  ProgramCounter programcounter_1 (
    .Clock(clock_1_out), .Reset(Reset_out), .Adress(programcounter_1_adress), .JMP(i_decode_1_jmp_address),
    .JMP_Flag(i_decode_1_jmp_flag), .Beq_Flag(i_decode_1_beq_flag));  // open: Adress__1
  TTY tty_1 (.data(i_decode_1_prnt_register), .clk(clock_1_out), .we(i_decode_1_prnt_flag), .clr(or_1_out));
  or or_1 (or_1_out, Reset_Display_out, i_decode_1_rst_flag);
  Keyboard keyboard_1 (.clk(clock_1_out));  // open: re, clr, avail, data
  RAM #(.addrWidth(16), .dataWidth(32), .bus("separate"), .Select("low")) ram_1 (
    .addr(programcounter_1_adress), .data({ram_1_data, ram_1_data_2}));  // open: din, str, sel, clk, ld, clr
  Register_part #(.Select("low")) register_1 (
    .D(ram_1_data[23:16]), .Q(register_1_q), .clk(clock_1_out), .clr(Reset_out));  // open: en
  Register_part #(.Select("low")) register_2 (
    .D(ram_1_data[15:8]), .Q(register_2_q), .clk(clock_1_out), .clr(Reset_out));  // open: en
  Register_part #(.Select("low")) register_3 (
    .D(ram_1_data_2), .Q(register_3_q), .clk(clock_1_out), .clr(Reset_out));  // open: en
  Register_part #(.Select("low")) register_4 (
    .D(ram_1_data[31:24]), .Q(register_4_q), .clk(clock_1_out), .clr(Reset_out));  // open: en
  I_Decode i_decode_1 (
    .Clock(clock_1_out), .Instruction(register_4_q), .Return_Register(register_1_q),
    .Arg1_Register(register_2_q), .Arg2_Register(register_3_q), .Reset(Reset_out),
    .JMP_Address(i_decode_1_jmp_address), .JMP_Flag(i_decode_1_jmp_flag), .BEQ_Flag(i_decode_1_beq_flag),
    .PRNT_Register(i_decode_1_prnt_register), .PRNT_FLag(i_decode_1_prnt_flag), .RST_Flag(i_decode_1_rst_flag));

  // Notes on the sheet:
  //   16-BIT CPU
  //   Keyboard
  //   Arguments
  //   Instruction
  //   Instrucotion decoder
endmodule

module ProgramCounter (
  input  JMP_Flag,
  input  [15:0] JMP,
  input  Clock,
  input  Reset,
  input  Beq_Flag,
  output [15:0] Adress,
  output [15:0] Adress__1
);

  wire not_1_out;
  wire [15:0] multiplexer_1_out, multiplexer_2_out;

  not not_1 (not_1_out, JMP_Flag);
  Multiplexer #(.width(16), .enable("false")) multiplexer_1 (
    .in0(JMP), .in1(Adress__1), .out(multiplexer_1_out), .sel(not_1_out));
  Register_part #(.width(16), .Select("low")) register_1 (
    .D(multiplexer_1_out), .Q(Adress), .clk(Clock), .clr(Reset));  // open: en
  Multiplexer #(.width(16), .enable("false")) multiplexer_2 (
    .in0(16'h1), .in1(16'h2), .out(multiplexer_2_out), .sel(Beq_Flag));
  Adder #(.width(16)) adder_1 (.a(Adress), .b(multiplexer_2_out), .out(Adress__1));  // open: cin, cout

  // Notes on the sheet:
  //   This module will point to an adress which executes the current instruction
endmodule

module I_Decode (
  input  Clock,
  input  Reset,
  input  [7:0] Instruction,
  input  [7:0] Return_Register,
  input  [7:0] Arg1_Register,
  input  [7:0] Arg2_Register,
  output [6:0] PRNT_Register,
  output JMP_Flag,
  output BEQ_Flag,
  output [15:0] JMP_Address,
  output PRNT_FLag,
  output RST_Flag
);

  wire alu_1_equals, and_1_out, and_2_out, and_4_out, and_5_out, and_8_out, and_9_out, and_10_out, not_1_out,
       or_1_out, or_2_out, or_3_out;
  wire [7:0] alu_1_output, register_1_q, register_2_q, register_controller_1_output_b_2, selector_1_output_a,
       selector_1_output_b, selector_1_output_c;
  wire [7:7] register_controller_1_output_a_2;

  or or_1 (or_1_out, Instruction[0], Instruction[1], Instruction[2], Instruction[3]);
  not not_1 (not_1_out, or_2_out);
  or or_2 (or_2_out, Instruction[4], Instruction[5], Instruction[6], Instruction[7]);
  and and_1 (and_1_out, Instruction[0], ~Instruction[1], ~Instruction[2], ~Instruction[3], Instruction[4], ~Instruction[5], ~Instruction[6], ~Instruction[7]);  // AND_Gate
  and and_2 (and_2_out, ~Instruction[0], Instruction[1], ~Instruction[2], ~Instruction[3], Instruction[4], ~Instruction[5], ~Instruction[6], ~Instruction[7]);  // AND_Gate
  and and_3 (JMP_Flag, ~Instruction[0], ~Instruction[1], ~Instruction[2], ~Instruction[3], Instruction[4], ~Instruction[5], ~Instruction[6], ~Instruction[7]);  // AND_Gate
  and and_4 (and_4_out, Instruction[0], ~Instruction[1], ~Instruction[2], ~Instruction[3], Instruction[4], ~Instruction[5], ~Instruction[6], ~Instruction[7]);  // AND_Gate
  and and_5 (and_5_out, ~Instruction[0], Instruction[1], ~Instruction[2], ~Instruction[3], Instruction[4], ~Instruction[5], ~Instruction[6], ~Instruction[7]);  // AND_Gate
  and and_6 (PRNT_FLag, Instruction[0], Instruction[1], ~Instruction[2], ~Instruction[3], Instruction[4], ~Instruction[5], ~Instruction[6], ~Instruction[7]);  // AND_Gate
  and and_7 (RST_Flag, ~Instruction[0], ~Instruction[1], Instruction[2], ~Instruction[3], Instruction[4], ~Instruction[5], ~Instruction[6], ~Instruction[7]);  // AND_Gate
  and and_8 (and_8_out, or_1_out, not_1_out);
  or or_3 (or_3_out, and_8_out, PRNT_FLag, and_1_out, and_2_out);
  selector selector_1 (
    .Selector(or_3_out), .Input_A(Return_Register), .Input_B(Arg1_Register), .Input_C(Arg2_Register),
    .Output_A(selector_1_output_a), .Output_B(selector_1_output_b), .Output_C(selector_1_output_c));
  selector selector_2 (
    .Selector(JMP_Flag), .Input_A(Return_Register), .Input_B(Arg1_Register), .Input_C(Arg2_Register),
    .Output_A(JMP_Address[15:8]), .Output_B(JMP_Address[7:0]));  // open: Output_C
  Register_part #(.Select("low")) register_1 (.D(selector_1_output_a), .Q(register_1_q), .clk(Clock));  // open: en, clr
  and and_9 (and_9_out, and_4_out, alu_1_equals);
  and and_10 (and_10_out, ~and_5_out, alu_1_equals);  // AND_Gate
  or or_4 (BEQ_Flag, and_9_out, and_10_out);
  Register_Controller register_controller_1 (
    .Clock(Clock), .Reset(Reset), .Output_A(selector_1_output_b), .Input_Adress(register_1_q),
    .Input_Data(register_2_q), .Output_B(selector_1_output_c),
    .Output_A_2({register_controller_1_output_a_2[7], PRNT_Register}),
    .Output_B_2(register_controller_1_output_b_2));
  ALU alu_1 (
    .Clock(Clock), .Instruction(Instruction), .Data_A({register_controller_1_output_a_2[7], PRNT_Register}),
    .Data_B(register_controller_1_output_b_2), .Output(alu_1_output), .Equals(alu_1_equals),
    .Data_Imidiate(selector_1_output_c));
  Register_part #(.Select("low")) register_2 (.D(alu_1_output), .Q(register_2_q), .clk(Clock));  // open: en, clr

  // Notes on the sheet:
  //   This module translates each instruction and requests data and arithmetic inputs
  //   BEQ
  //   BEQ
  //   BNEQ
  //   PRNT
  //   RST
  //   JMP
  //   ALL Instructions with 0000 0001 -> 0000 1111 are related to ALU
  //   Register
  //   ALU
  //   Write-Back Register
endmodule

module ALU (
  input  Clock,
  input  [7:0] Instruction,
  input  [7:0] Data_A,
  input  [7:0] Data_B,
  input  [7:0] Data_Imidiate,
  output [7:0] Output,
  output Equals
);

  wire [7:0] adder_1_out, adder_2_out, divider_1_out, divider_2_out, multiplier_1_out, multiplier_2_out,
       subtractor_1_out, subtractor_2_out;

  Adder adder_1 (.a(Data_A), .b(Data_B), .out(adder_1_out));  // open: cin, cout
  Adder adder_2 (.a(Data_A), .b(Data_Imidiate), .out(adder_2_out));  // open: cin, cout
  Subtractor subtractor_1 (.a(Data_A), .b(Data_B), .out(subtractor_1_out));  // open: bin, bout
  Subtractor subtractor_2 (.a(Data_A), .b(Data_Imidiate), .out(subtractor_2_out));  // open: bin, bout
  Multiplier multiplier_1 (.a(Data_A), .b(Data_B), .out(multiplier_1_out));  // open: cin, cout
  Multiplier multiplier_2 (.a(Data_A), .b(Data_Imidiate), .out(multiplier_2_out));  // open: cin, cout
  Divider divider_1 (.a(Data_A), .b(Data_B), .out(divider_1_out));  // open: upper, rem
  Divider divider_2 (.a(Data_A), .b(Data_Imidiate), .out(divider_2_out));  // open: upper, rem
  Comparator comparator_1 (.a(Data_A), .b(Data_B), .eq(Equals));  // open: gt, lt
  Multiplexer #(.select(4), .width(8), .enable("false")) multiplexer_1 (
    .in0({8{1'b0}}), .in1(adder_1_out), .in2(adder_2_out), .in3(subtractor_1_out), .in4(subtractor_2_out),
    .in5(multiplier_1_out), .in6(multiplier_2_out), .in7(divider_1_out), .in8(divider_2_out), .out(Output),
    .sel(Instruction[3:0]));  // open: in9, in10, in11, in12, in13, in14, in15

  // Notes on the sheet:
  //   Instructions with registers only
endmodule

module Register (
  input  Clock,
  input  Reset,
  input  [7:0] Adress,
  input  [7:0] Adress_Output,
  input  [7:0] Data_A,
  output [7:0] out_6
);

  wire demultiplexer_2_out1, demultiplexer_2_out2, demultiplexer_2_out3, demultiplexer_2_out4,
       demultiplexer_2_out5, demultiplexer_2_out6, demultiplexer_2_out7, demultiplexer_2_out8,
       demultiplexer_2_out9, demultiplexer_2_out10, demultiplexer_2_out11, demultiplexer_2_out12,
       demultiplexer_2_out13, demultiplexer_2_out14, demultiplexer_2_out15;
  wire [7:0] demultiplexer_1_out1, demultiplexer_1_out2, demultiplexer_1_out3, demultiplexer_1_out4,
       demultiplexer_1_out5, demultiplexer_1_out6, demultiplexer_1_out7, demultiplexer_1_out8,
       demultiplexer_1_out9, demultiplexer_1_out10, demultiplexer_1_out11, demultiplexer_1_out12,
       demultiplexer_1_out13, demultiplexer_1_out14, demultiplexer_1_out15, register_1_q, register_2_q,
       register_3_q, register_5_q, register_6_q, register_7_q, register_8_q, register_9_q, register_10_q,
       register_11_q, register_12_q, register_13_q, register_14_q, register_15_q;

  Demultiplexer #(.select(4), .width(8), .enable("false")) demultiplexer_1 (
    .out1(demultiplexer_1_out1), .out2(demultiplexer_1_out2), .out3(demultiplexer_1_out3),
    .out4(demultiplexer_1_out4), .out5(demultiplexer_1_out5), .out6(demultiplexer_1_out6),
    .out7(demultiplexer_1_out7), .out8(demultiplexer_1_out8), .out9(demultiplexer_1_out9),
    .out10(demultiplexer_1_out10), .out11(demultiplexer_1_out11), .out12(demultiplexer_1_out12),
    .out13(demultiplexer_1_out13), .out14(demultiplexer_1_out14), .out15(demultiplexer_1_out15), .in(Data_A),
    .sel(Adress[3:0]));  // open: out0
  Demultiplexer #(.select(4), .enable("false")) demultiplexer_2 (
    .out1(demultiplexer_2_out1), .out2(demultiplexer_2_out2), .out3(demultiplexer_2_out3),
    .out4(demultiplexer_2_out4), .out5(demultiplexer_2_out5), .out6(demultiplexer_2_out6),
    .out7(demultiplexer_2_out7), .out8(demultiplexer_2_out8), .out9(demultiplexer_2_out9),
    .out10(demultiplexer_2_out10), .out11(demultiplexer_2_out11), .out12(demultiplexer_2_out12),
    .out13(demultiplexer_2_out13), .out14(demultiplexer_2_out14), .out15(demultiplexer_2_out15), .in(1'b1),
    .sel(Adress[3:0]));  // open: out0
  Register_part #(.Select("low")) register_1 (
    .D(demultiplexer_1_out1), .en(demultiplexer_2_out1), .Q(register_1_q), .clk(Clock), .clr(Reset));
  Register_part #(.Select("low")) register_2 (
    .D(demultiplexer_1_out2), .en(demultiplexer_2_out2), .Q(register_2_q), .clk(Clock), .clr(Reset));
  Register_part #(.Select("low")) register_3 (
    .D(demultiplexer_1_out3), .en(demultiplexer_2_out3), .Q(register_3_q), .clk(Clock), .clr(Reset));
  Register_part #(.Select("low")) register_4 (
    .D(demultiplexer_1_out4), .en(demultiplexer_2_out4), .Q(register_3_q), .clk(Clock), .clr(Reset));
  Register_part #(.Select("low")) register_5 (
    .D(demultiplexer_1_out5), .en(demultiplexer_2_out5), .Q(register_5_q), .clk(Clock), .clr(Reset));
  Register_part #(.Select("low")) register_6 (
    .D(demultiplexer_1_out6), .en(demultiplexer_2_out6), .Q(register_6_q), .clk(Clock), .clr(Reset));
  Register_part #(.Select("low")) register_7 (
    .D(demultiplexer_1_out7), .en(demultiplexer_2_out7), .Q(register_7_q), .clk(Clock), .clr(Reset));
  Register_part #(.Select("low")) register_8 (
    .D(demultiplexer_1_out8), .en(demultiplexer_2_out8), .Q(register_8_q), .clk(Clock), .clr(Reset));
  Register_part #(.Select("low")) register_9 (
    .D(demultiplexer_1_out9), .en(demultiplexer_2_out9), .Q(register_9_q), .clk(Clock), .clr(Reset));
  Register_part #(.Select("low")) register_10 (
    .D(demultiplexer_1_out10), .en(demultiplexer_2_out10), .Q(register_10_q), .clk(Clock), .clr(Reset));
  Register_part #(.Select("low")) register_11 (
    .D(demultiplexer_1_out11), .en(demultiplexer_2_out11), .Q(register_11_q), .clk(Clock), .clr(Reset));
  Register_part #(.Select("low")) register_12 (
    .D(demultiplexer_1_out12), .en(demultiplexer_2_out12), .Q(register_12_q), .clk(Clock), .clr(Reset));
  Register_part #(.Select("low")) register_13 (
    .D(demultiplexer_1_out13), .en(demultiplexer_2_out13), .Q(register_13_q), .clk(Clock), .clr(Reset));
  Register_part #(.Select("low")) register_14 (
    .D(demultiplexer_1_out14), .en(demultiplexer_2_out14), .Q(register_14_q), .clk(Clock), .clr(Reset));
  Register_part #(.Select("low")) register_15 (
    .D(demultiplexer_1_out15), .en(demultiplexer_2_out15), .Q(register_15_q), .clk(Clock), .clr(Reset));
  Multiplexer #(.select(4), .width(8), .enable("false")) multiplexer_1 (
    .in0({8{1'b0}}), .in1(register_1_q), .in2(register_2_q), .in3(register_3_q), .in4(register_3_q),
    .in5(register_5_q), .in6(register_6_q), .in7(register_7_q), .in8(register_8_q), .in9(register_9_q),
    .in10(register_10_q), .in11(register_11_q), .in12(register_12_q), .in13(register_13_q),
    .in14(register_14_q), .in15(register_15_q), .out(out_6), .sel(Adress_Output[3:0]));

  // Notes on the sheet:
  //   Register 1
endmodule

module Register_Controller (
  input  Clock,
  input  Reset,
  input  [7:0] Output_A,
  input  [7:0] Input_Adress,
  input  [7:0] Input_Data,
  input  [7:0] Output_B,
  output [7:0] Output_A_2,
  output [7:0] Output_B_2
);

  Register register_1 (
    .Clock(Clock), .Reset(Reset), .Adress(Input_Adress), .Adress_Output(Output_A), .Data_A(Input_Data),
    .out_6(Output_A_2));
  Register register_2 (
    .Clock(Clock), .Reset(Reset), .Adress(Input_Adress), .Adress_Output(Output_B), .Data_A(Input_Data),
    .out_6(Output_B_2));
endmodule

module selector (
  input  Selector,
  input  [7:0] Input_A,
  input  [7:0] Input_B,
  input  [7:0] Input_C,
  output [7:0] Output_A,
  output [7:0] Output_B,
  output [7:0] Output_C
);

  wire [7:0] demultiplexer_2_out0;

  Demultiplexer #(.width(8), .enable("false")) demultiplexer_1 (
    .out1(Output_A), .in(Input_A), .sel(Selector));  // open: out0
  Demultiplexer #(.width(8), .enable("false")) demultiplexer_2 (
    .out0(demultiplexer_2_out0), .out1(Output_B), .in(Input_B), .sel(Selector));
  Demultiplexer #(.width(8), .enable("false")) demultiplexer_3 (
    .out1(Output_C), .in(Input_C), .sel(Selector));  // open: out0
endmodule
